// Logisim project logiproj.circ as structural Verilog: 1 circuit, main circuit main
module main (
  input  in_1,
  input  in_2,
  input  in_3,
  input  in_4,
  input  in_5,
  input  in_6,
  input  in_7,
  input  in_8,
  input  in_9,
  input  in_10,
  input  in_11,
  input  in_12,
  input  in_13,
  input  in_14,
  output out_15,
  output out_16,
  output out_17,
  output out_18,
  output out_19,
  output out_20,
  output out_21,
  output out_22,
  output out_23,
  output out_24,
  output out_25,
  output out_26,
  output A,
  output out_28,
  output B,
  output out_30,
  output out_31,
  output out_32,
  output out_33,
  output out_34,
  output out_35,
  output out_36,
  output out_37,
  output out_38,
  output out_39,
  output out_40
);

  wire and_1_out, and_2_out, and_3_out, and_4_out, and_5_out, and_6_out, button_1_out, button_2_out,
       button_3_out, button_4_out, button_5_out, button_6_out, button_7_out, button_8_out, button_9_out,
       button_10_out, button_11_out, clock_1_out, clock_2_out, d_ff_1_q, d_ff_2_q, d_ff_3_q, d_ff_4_q,
       d_ff_5_q, d_ff_6_q, d_ff_7_q, d_ff_8_q, d_ff_9_q, d_ff_10_q, d_ff_11_q, d_ff_12_q, d_ff_13_q,
       d_ff_14_q, d_ff_15_q, d_ff_16_q, d_ff_17_q, d_ff_18_q, d_ff_19_q, d_ff_20_q, d_ff_20_qn, d_ff_21_q,
       d_ff_22_q, d_ff_22_qn, d_ff_23_q, d_ff_25_q, demultiplexer_1_out0, demultiplexer_1_out1,
       demultiplexer_2_out0, demultiplexer_2_out1, demultiplexer_3_out0, demultiplexer_3_out1,
       demultiplexer_4_out0, demultiplexer_4_out1, demultiplexer_5_out0, demultiplexer_5_out1,
       demultiplexer_6_out0, demultiplexer_6_out1, demultiplexer_7_out0, demultiplexer_7_out1,
       demultiplexer_8_out0, demultiplexer_8_out1, demultiplexer_9_out0, demultiplexer_9_out1,
       demultiplexer_11_out0, demultiplexer_11_out1, nand_1_out, nor_1_out, nor_2_out, nor_3_out, nor_4_out,
       not_1_out, or_1_out, or_2_out, or_3_out, or_4_out, or_5_out, or_6_out, or_7_out, or_8_out, or_9_out,
       or_10_out, or_11_out, or_12_out, or_13_out, or_14_out, or_15_out, or_16_out, or_17_out, undriven,
       undriven_2, undriven_3, undriven_4, undriven_5, undriven_6, undriven_7, undriven_8, undriven_9,
       xor_1_out, xor_2_out, xor_3_out;

  Demultiplexer demultiplexer_1 (
    .out0(demultiplexer_1_out0), .out1(demultiplexer_1_out1), .in(1'b1), .sel(in_5), .en(1'b1));
  Demultiplexer demultiplexer_2 (
    .out0(demultiplexer_2_out0), .out1(demultiplexer_2_out1), .in(1'b1), .sel(in_9), .en(1'b1));
  Demultiplexer demultiplexer_3 (
    .out0(demultiplexer_3_out0), .out1(demultiplexer_3_out1), .in(1'b1), .sel(in_12), .en(1'b1));
  D_Flip_Flop d_ff_1 (
    .clk(button_1_out), .D(demultiplexer_1_out1), .Q(d_ff_1_q), .reset(not_1_out));  // open: Qn, preset, en
  D_Flip_Flop d_ff_2 (
    .clk(button_2_out), .D(demultiplexer_2_out1), .Q(d_ff_2_q), .reset(not_1_out));  // open: Qn, preset, en
  D_Flip_Flop d_ff_3 (
    .clk(button_3_out), .D(demultiplexer_3_out1), .Q(d_ff_3_q), .reset(not_1_out));  // open: Qn, preset, en
  Button button_1 (.out(button_1_out));
  Button button_2 (.out(button_2_out));
  Button button_3 (.out(button_3_out));
  D_Flip_Flop d_ff_4 (
    .clk(button_1_out), .D(demultiplexer_1_out0), .Q(d_ff_4_q), .reset(not_1_out));  // open: Qn, preset, en
  D_Flip_Flop d_ff_5 (
    .clk(button_2_out), .D(demultiplexer_2_out0), .Q(d_ff_5_q), .reset(not_1_out));  // open: Qn, preset, en
  D_Flip_Flop d_ff_6 (
    .clk(button_3_out), .D(demultiplexer_3_out0), .Q(d_ff_6_q), .reset(not_1_out));  // open: Qn, preset, en
  LED led_1 (.in(or_5_out));
  Button button_4 (.out(button_4_out));
  Demultiplexer demultiplexer_4 (
    .out0(demultiplexer_4_out0), .out1(demultiplexer_4_out1), .in(1'b1), .sel(in_6), .en(1'b1));
  Demultiplexer demultiplexer_5 (
    .out0(demultiplexer_5_out0), .out1(demultiplexer_5_out1), .in(1'b1), .sel(in_10), .en(1'b1));
  Demultiplexer demultiplexer_6 (
    .out0(demultiplexer_6_out0), .out1(demultiplexer_6_out1), .in(1'b1), .sel(in_13), .en(1'b1));
  Button button_5 (.out(button_5_out));
  Button button_6 (.out(button_6_out));
  Button button_7 (.out(button_7_out));
  or or_1 (or_1_out, button_4_out, button_1_out, button_2_out, button_3_out, button_5_out, button_6_out, button_7_out, button_8_out, button_9_out, button_10_out);
  Button button_8 (.out(button_8_out));
  Button button_9 (.out(button_9_out));
  Button button_10 (.out(button_10_out));
  D_Flip_Flop d_ff_7 (
    .clk(button_5_out), .D(demultiplexer_4_out1), .Q(d_ff_7_q), .reset(not_1_out));  // open: Qn, preset, en
  D_Flip_Flop d_ff_8 (
    .clk(button_5_out), .D(demultiplexer_4_out0), .Q(d_ff_8_q), .reset(not_1_out));  // open: Qn, preset, en
  D_Flip_Flop d_ff_9 (
    .clk(button_6_out), .D(demultiplexer_5_out1), .Q(d_ff_9_q), .reset(not_1_out));  // open: Qn, preset, en
  D_Flip_Flop d_ff_10 (
    .clk(button_6_out), .D(demultiplexer_5_out0), .Q(d_ff_10_q), .reset(not_1_out));  // open: Qn, preset, en
  D_Flip_Flop d_ff_11 (
    .clk(button_7_out), .D(demultiplexer_6_out1), .Q(d_ff_11_q), .reset(not_1_out));  // open: Qn, preset, en
  D_Flip_Flop d_ff_12 (
    .clk(button_7_out), .D(demultiplexer_6_out0), .Q(d_ff_12_q), .reset(not_1_out));  // open: Qn, preset, en
  Demultiplexer demultiplexer_7 (
    .out0(demultiplexer_7_out0), .out1(demultiplexer_7_out1), .in(1'b1), .sel(in_7), .en(1'b1));
  Demultiplexer demultiplexer_8 (
    .out0(demultiplexer_8_out0), .out1(demultiplexer_8_out1), .in(1'b1), .sel(in_11), .en(1'b1));
  Demultiplexer demultiplexer_9 (
    .out0(demultiplexer_9_out0), .out1(demultiplexer_9_out1), .in(1'b1), .sel(in_14), .en(1'b1));
  D_Flip_Flop d_ff_13 (
    .clk(button_8_out), .D(demultiplexer_7_out1), .Q(d_ff_13_q), .reset(not_1_out));  // open: Qn, preset, en
  D_Flip_Flop d_ff_14 (
    .clk(button_8_out), .D(demultiplexer_7_out0), .Q(d_ff_14_q), .reset(not_1_out));  // open: Qn, preset, en
  D_Flip_Flop d_ff_15 (
    .clk(button_9_out), .D(demultiplexer_8_out1), .Q(d_ff_15_q), .reset(not_1_out));  // open: Qn, preset, en
  D_Flip_Flop d_ff_16 (
    .clk(button_9_out), .D(demultiplexer_8_out0), .Q(d_ff_16_q), .reset(not_1_out));  // open: Qn, preset, en
  D_Flip_Flop d_ff_17 (
    .clk(button_10_out), .D(demultiplexer_9_out1), .Q(d_ff_17_q), .reset(not_1_out));  // open: Qn, preset, en
  D_Flip_Flop d_ff_18 (
    .clk(button_10_out), .D(demultiplexer_9_out0), .Q(d_ff_18_q), .reset(not_1_out));  // open: Qn, preset, en
  and and_1 (and_1_out, d_ff_22_q, d_ff_21_q, d_ff_20_q);
  and and_2 (and_2_out, d_ff_21_q, d_ff_22_q);
  xor xor_1 (xor_1_out, d_ff_19_q, and_1_out);
  xor xor_2 (xor_2_out, d_ff_20_q, and_2_out);
  xor xor_3 (xor_3_out, d_ff_21_q, d_ff_22_q);
  nand nand_1 (nand_1_out, d_ff_19_q, d_ff_20_qn, d_ff_21_q, d_ff_22_qn);
  and and_3 (and_3_out, xor_1_out, nand_1_out);
  and and_4 (and_4_out, xor_2_out, nand_1_out);
  and and_5 (and_5_out, xor_3_out, nand_1_out);
  and and_6 (and_6_out, nand_1_out, d_ff_22_qn);
  _7_Segment_Display u_7_segment_display_1 (
    .g(d_ff_1_q), .f(or_2_out), .a(d_ff_4_q), .b(or_2_out), .e(or_2_out), .d(d_ff_4_q), .c(or_2_out));  // open: dp
  or or_2 (or_2_out, d_ff_1_q, d_ff_4_q);
  _7_Segment_Display u_7_segment_display_2 (
    .g(d_ff_2_q), .f(or_3_out), .a(d_ff_5_q), .b(or_3_out), .e(or_3_out), .d(d_ff_5_q), .c(or_3_out));  // open: dp
  or or_3 (or_3_out, d_ff_2_q, d_ff_5_q);
  _7_Segment_Display u_7_segment_display_3 (
    .g(d_ff_3_q), .f(or_4_out), .a(d_ff_6_q), .b(or_4_out), .e(or_4_out), .d(d_ff_6_q), .c(or_4_out));  // open: dp
  or or_4 (or_4_out, d_ff_3_q, d_ff_6_q);
  D_Flip_Flop d_ff_19 (.clk(or_1_out), .D(and_3_out), .Q(d_ff_19_q), .reset(or_12_out));  // open: Qn, preset, en
  D_Flip_Flop d_ff_20 (
    .clk(or_1_out), .D(and_4_out), .Q(d_ff_20_q), .Qn(d_ff_20_qn), .reset(or_12_out));  // open: preset, en
  D_Flip_Flop d_ff_21 (.clk(or_1_out), .D(and_5_out), .Q(d_ff_21_q), .reset(or_12_out));  // open: Qn, preset, en
  D_Flip_Flop d_ff_22 (
    .clk(or_1_out), .D(and_6_out), .Q(d_ff_22_q), .Qn(d_ff_22_qn), .reset(or_12_out));  // open: preset, en
  not not_1 (not_1_out, or_5_out);
  or or_5 (or_5_out, d_ff_19_q, d_ff_20_q, d_ff_21_q, d_ff_22_q);
  _7_Segment_Display u_7_segment_display_4 (
    .g(d_ff_7_q), .f(or_6_out), .a(d_ff_8_q), .b(or_6_out), .e(or_6_out), .d(d_ff_8_q), .c(or_6_out));  // open: dp
  or or_6 (or_6_out, d_ff_7_q, d_ff_8_q);
  _7_Segment_Display u_7_segment_display_5 (
    .g(d_ff_9_q), .f(or_7_out), .a(d_ff_10_q), .b(or_7_out), .e(or_7_out), .d(d_ff_10_q), .c(or_7_out));  // open: dp
  or or_7 (or_7_out, d_ff_9_q, d_ff_10_q);
  _7_Segment_Display u_7_segment_display_6 (
    .g(d_ff_11_q), .f(or_8_out), .a(d_ff_12_q), .b(or_8_out), .e(or_8_out), .d(d_ff_12_q), .c(or_8_out));  // open: dp
  or or_8 (or_8_out, d_ff_11_q, d_ff_12_q);
  _7_Segment_Display u_7_segment_display_7 (
    .g(d_ff_13_q), .f(or_9_out), .a(d_ff_14_q), .b(or_9_out), .e(or_9_out), .d(d_ff_14_q), .c(or_9_out));  // open: dp
  or or_9 (or_9_out, d_ff_13_q, d_ff_14_q);
  _7_Segment_Display u_7_segment_display_8 (
    .g(d_ff_15_q), .f(or_10_out), .a(d_ff_16_q), .b(or_10_out), .e(or_10_out), .d(d_ff_16_q), .c(or_10_out));  // open: dp
  or or_10 (or_10_out, d_ff_15_q, d_ff_16_q);
  _7_Segment_Display u_7_segment_display_9 (
    .g(d_ff_17_q), .f(or_11_out), .a(d_ff_18_q), .b(or_11_out), .e(or_11_out), .d(d_ff_18_q), .c(or_11_out));  // open: dp
  or or_11 (or_11_out, d_ff_17_q, d_ff_18_q);
  Button button_11 (.out(button_11_out));
  or or_12 (or_12_out, button_11_out, or_15_out);
  and and_7 (out_17, d_ff_1_q, d_ff_7_q, d_ff_13_q);
  and and_8 (out_19, d_ff_2_q, d_ff_9_q, d_ff_15_q);
  and and_9 (out_21, d_ff_3_q, d_ff_11_q, d_ff_17_q);
  and and_10 (out_23, d_ff_1_q, d_ff_2_q, d_ff_3_q);
  and and_11 (out_25, d_ff_7_q, d_ff_9_q, d_ff_11_q);
  and and_12 (out_28, d_ff_13_q, d_ff_15_q, d_ff_17_q);
  and and_13 (out_31, d_ff_1_q, d_ff_9_q, d_ff_17_q);
  and and_14 (out_32, d_ff_13_q, d_ff_9_q, d_ff_3_q);
  and and_15 (out_33, d_ff_4_q, d_ff_8_q, d_ff_14_q);
  and and_16 (out_34, d_ff_5_q, d_ff_10_q, d_ff_16_q);
  and and_17 (out_35, d_ff_6_q, d_ff_12_q, d_ff_18_q);
  and and_18 (out_36, d_ff_4_q, d_ff_5_q, d_ff_6_q);
  and and_19 (out_37, d_ff_8_q, d_ff_10_q, d_ff_12_q);
  and and_20 (out_38, d_ff_14_q, d_ff_16_q, d_ff_18_q);
  and and_21 (out_39, d_ff_4_q, d_ff_10_q, d_ff_18_q);
  and and_22 (out_40, d_ff_14_q, d_ff_10_q, d_ff_6_q);
  nor nor_1 (nor_1_out, or_1_out, nor_2_out);
  nor nor_2 (nor_2_out, nor_1_out, or_13_out);
  or or_13 (or_13_out, out_17, out_19, out_21, out_23, out_25, out_28, out_31, out_32);
  nor nor_3 (nor_3_out, or_1_out, nor_4_out);
  nor nor_4 (nor_4_out, nor_3_out, or_14_out);
  or or_14 (or_14_out, out_33, out_34, out_35, out_36, out_37, out_38, out_39, out_40);
  LED led_2 (.in(nor_1_out));
  LED led_3 (.in(nor_1_out));
  LED led_4 (.in(nor_1_out));
  LED led_5 (.in(nor_1_out));
  LED led_6 (.in(nor_3_out));
  LED led_7 (.in(nor_3_out));
  LED led_8 (.in(nor_3_out));
  or or_15 (or_15_out, nor_1_out, nor_3_out);
  LED led_9 (.in(nor_1_out));
  LED led_10 (.in(nor_1_out));
  LED led_11 (.in(nor_1_out));
  LED led_12 (.in(nor_1_out));
  LED led_13 (.in(nor_1_out));
  LED led_14 (.in(nor_3_out));
  LED led_15 (.in(nor_3_out));
  LED led_16 (.in(nor_3_out));
  LED led_17 (.in(nor_3_out));
  LED led_18 (.in(nor_3_out));
  LED led_19 (.in(nor_3_out));
  LED led_20 (.in(nor_3_out));
  LED led_21 (.in(nor_3_out));
  LED led_22 (.in(nor_3_out));
  and and_23 (out_15, undriven_9, undriven_8, undriven_7);
  and and_24 (out_16, undriven_6, undriven_5, undriven_4);
  and and_25 (out_18, undriven_3, undriven_2, undriven);
  and and_26 (out_20, undriven_9, undriven_6, undriven_3);
  and and_27 (out_22, undriven_8, undriven_5, undriven_2);
  and and_28 (out_24, undriven_7, undriven_4, undriven);
  and and_29 (out_26, undriven_9, undriven_5, undriven);
  and and_30 (out_30, undriven_7, undriven_5, undriven_3);
  Demultiplexer demultiplexer_10 (.out0(A), .out1(B), .in(in_1), .sel(in_3), .en(in_2));
  Clock clock_1 (.out(clock_1_out));
  Demultiplexer demultiplexer_11 (
    .out0(demultiplexer_11_out0), .out1(demultiplexer_11_out1), .in(1'b1), .en(1'b1));  // open: sel
  Clock clock_2 (.out(clock_2_out));
  D_Flip_Flop d_ff_23 (
    .clk(clock_1_out), .D(demultiplexer_11_out1), .Q(d_ff_23_q), .reset(in_8));  // open: Qn, preset, en
  or or_16 (or_16_out, A, B);
  D_Flip_Flop d_ff_24 (.clk(clock_2_out), .D(A), .reset(in_4));  // open: Q, Qn, preset, en
  D_Flip_Flop d_ff_25 (
    .clk(clock_1_out), .D(demultiplexer_11_out0), .Q(d_ff_25_q), .reset(in_8));  // open: Qn, preset, en
  _7_Segment_Display u_7_segment_display_10 (
    .g(A), .f(or_16_out), .a(B), .b(or_16_out), .e(or_16_out), .d(B), .c(or_16_out));  // open: dp
  D_Flip_Flop d_ff_26 (.clk(clock_2_out), .D(B), .reset(in_4));  // open: Q, Qn, preset, en
  _7_Segment_Display u_7_segment_display_11 (
    .g(d_ff_23_q), .f(or_17_out), .a(d_ff_25_q), .b(or_17_out), .e(or_17_out), .d(d_ff_25_q), .c(or_17_out));  // open: dp
  or or_17 (or_17_out, d_ff_23_q, d_ff_25_q);

  // Notes on the sheet:
  //   CONTROLS
  //   X  = 1
  //   O = 0
  //   INITIALIZE
  //   RESET
endmodule
